# Fritzing sketch wurka.001 (saved by Fritzing 0.9.3b)
circuit board: 21.6723cm x 7.37331cm
breadboards: 1

parts:
  Part1 = Arduino Uno (Rev3)
  Squix1 = OLED 0.96" 128x64 I2C SSD1306
  RHT1 = Humidity and Temperature Sensor RHT03 [part_number="ASAIR AM2302 DHT22 SNK118230B27D"]
  U1 = Sharp PC817 [package=THT]
  S1 = Taiway 100-SP-X-T1 SPDT Miniature Toggle Switch [part_number=100-SP-X-T1-0-0-B1-M2 package=THT]
  U3 = RELAY [package=relay-jzc]
  R1 = Resistor [tolerance=±1% resistance=1k package=THT]
  Q1 = NPN-Transistor [part_number=BC548 package="TO92 [THT]"]
  LED1 = LED - 5mm [color="Red (633nm)" package="5 mm [THT]"]
  HEATER = Camdenboss CTB0158-2 [part_number=CTB0158-2 package=THT]
  R2 = Resistor [tolerance=±1% resistance=1k package=THT]
  R3 = Resistor [tolerance=±1% resistance=1k package=THT]
  R4 = Resistor [tolerance=±1% resistance=1k package=THT]
  U4 = RELAY [package=relay-jzc]
  Q2 = NPN-Transistor [part_number=BC548 package="TO92 [THT]"]
  LED2 = LED - 5mm [color="Red (633nm)" package="5 mm [THT]"]
  DIFFUSOR_POWER = Camdenboss CTB0158-2 [part_number=CTB0158-2 package=THT]
  R5 = Resistor [tolerance=±5% resistance=220 package=THT]
  DIFFUSOR_CONTROLE = Camdenboss CTB0158-2 [part_number=CTB0158-2 package=THT]
  FAN = Camdenboss CTB0158-2 [part_number=CTB0158-2 package=THT]
  Power_plug1 = Power plug
  ALARM = Camdenboss CTB0158-2 [part_number=CTB0158-2 package=THT]
  R6 = Resistor [tolerance=±5% resistance=6.8k package=THT]
  ENCODER1 = Rotary Encoder with Knob

nets:
  N1: Part1.A4/SDA, Squix1.SCA
  N2: Part1.A5/SCL, Squix1.SCL
  N3: Part1.D9_PWM, R1.Pin_1
  N4: Part1.D11_PWM/MOSI, R3.Pin_1
  N5: Part1.D12/MISO, FAN.pin1
  N6: Part1.D13/SCK, R5.Pin_1
  GND: Part1.GND, Squix1.GND, RHT1.GND_2, U1.Pin_2, Q1.C, Q2.C, FAN.pin2, Power_plug1.GND, ALARM.pin2, ENCODER1.GND
  N7: Part1.D2, ENCODER1.CLK
  N8: Part1.D3_PWM, ENCODER1.DT
  N9: Part1.D4, ENCODER1.SW
  N10: Part1.D6_PWM, ALARM.pin1
  VCC: Part1.5V, Squix1.VCC, RHT1.Vcc, U3.COIL1, R2.Pin_0, R4.Pin_0, U4.COIL1, R6.Pin_0, ENCODER1.VCC
  N11: Part1.VIN, S1.L1
  N12: RHT1.Data-signal, R6.Pin_1
  N13: U1.Pin_1, R5.Pin_0
  N14: U1.Pin_4, DIFFUSOR_CONTROLE.pin1
  N15: U1.Pin_3, DIFFUSOR_CONTROLE.pin2
  N16: S1.L2, Power_plug1.VCC
  N17: U3.COIL2, Q1.E, LED1.cathode
  N18: U3.NO, HEATER.pin2
  N19: U3.MAIN, HEATER.pin1
  N20: R1.Pin_0, Q1.B
  N21: LED1.anode, R2.Pin_1
  N22: R3.Pin_0, Q2.B
  N23: R4.Pin_1, LED2.anode
  N24: U4.COIL2, Q2.E, LED2.cathode
  N25: U4.NO, DIFFUSOR_POWER.pin2
  N26: U4.MAIN, DIFFUSOR_POWER.pin1

custom parts:
  Rotary Encoder with Knob: Rotary Encoder with 1/4" Shaft and Knob
