# Fritzing sketch wurka (saved by Fritzing 0.9.3b)
circuit board: 21.6723cm x 7.37331cm
breadboards: 1

parts:
  Part1 = Arduino Uno (Rev3)
  Squix1 = OLED 0.96" 128x64 I2C SSD1306
  RE1 = Rotary Encoder [package=THT]  # not connected
  RHT1 = Humidity and Temperature Sensor RHT03  # not connected
  RHT2 = Humidity and Temperature Sensor RHT03  # not connected

nets:
  N1: Part1.A4/SDA, Squix1.SCA
  N2: Part1.A5/SCL, Squix1.SCL
  5V: Part1.5V, Squix1.VCC
  GND: Part1.GND, Squix1.GND
